# Fritzing sketch BreadboardSketch (saved by Fritzing 0.9.3b)
breadboards: 2

parts:
  U1 = NodeMCU V3.0
  Squix1 = OLED 0.96" 128x64 I2C SSD1306
  R1 = Resistor [tolerance=±5% resistance=220 package=THT]
  LED1 = LED - 5mm [color="Red (633nm)" package="5 mm [THT]"]
  R2 = PHOTOCELL [package=photocell-kit]
  R3 = Resistor [tolerance=±5% resistance=10k package=THT]

nets:
  3V3: U1.3V3, Squix1.VCC, R2.P$2
  N1: U1.GND#6, U1.GND#13, U1.GND#16, U1.GND#33, Squix1.GND, R1.Pin_1
  N2: U1.D5, Squix1.SCL
  N3: U1.D6, Squix1.SCA
  N4: U1.D8, LED1.anode
  N5: U1.GND#41, R3.Pin_0
  N6: U1.A0, R2.P$1, R3.Pin_1
  N7: R1.Pin_0, LED1.cathode

notes:
  Remove one of the side rails to allow two half-size breadboards side-by-side.
  Build pushbutton switch out of paperclips, a bit of aluminum foil, and a piece of cardstock! (Or just tap the wires together.) Requires gpio.PULLUP enabled!
  Read the labels! 3V to Vcc; G to Gnd. Don't trust pin position.

custom parts:
  NodeMCU V3.0: ESP8266 based NodeMCU
